// Logisim project Slot Machine.circ as structural Verilog
module main (
  input  IsEasy,
  output F,
  output G,
  output A,
  output B,
  output C,
  output D,
  output E,
  output E0,
  output E1,
  output E2,
  output E3
);

  wire clock_1_out, demultiplexer_1_out0, demultiplexer_1_out1, demultiplexer_2_out0, demultiplexer_2_out1,
       easymode_1_stop_out, hardmode_1_stop_out, jackpot_1_outp, multiplexer_4_out, n7447_1_pin3, Start_out,
       Stop_out;
  wire [1:0] counter1_1_out1;
  wire [3:0] easymode_1_n1, easymode_1_n2, easymode_1_n3, hardmode_1_n1, hardmode_1_n2, hardmode_1_n3,
       multiplexer_1_out, multiplexer_2_out, multiplexer_3_out, multiplexer_5_out;

  Button Start (.out(Start_out));
  Clock clock_1 (.out(clock_1_out));
  Button Stop (.out(Stop_out));
  Demultiplexer demultiplexer_1 (
    .out0(demultiplexer_1_out0), .out1(demultiplexer_1_out1), .in(Start_out), .sel(IsEasy));
  Demultiplexer demultiplexer_2 (.out0(demultiplexer_2_out0), .out1(demultiplexer_2_out1), .in(Stop_out), .sel(IsEasy));
  counter1 counter1_1 (.Clock(clock_1_out), .Out1(counter1_1_out1[0]), .Out2(counter1_1_out1[1]));
  Demultiplexer #(.enable("true"), .select(2)) demultiplexer_3 (
    .out0(E0), .out1(E1), .out2(E2), .out3(E3), .in(1'b1), .sel(counter1_1_out1), .en(1'b1));
  hardmode hardmode_1 (
    .Start(demultiplexer_1_out0), .Clk(clock_1_out), .Stop(demultiplexer_2_out0), .N1(hardmode_1_n1),
    .N2(hardmode_1_n2), .N3(hardmode_1_n3), .stop_out(hardmode_1_stop_out));
  easymode easymode_1 (
    .Start(demultiplexer_1_out1), .Clk(clock_1_out), .Stop(demultiplexer_2_out1), .N1(easymode_1_n1),
    .N2(easymode_1_n2), .N3(easymode_1_n3), .stop_out(easymode_1_stop_out));
  Multiplexer #(.width(4)) multiplexer_1 (
    .in0(hardmode_1_n1), .in1(easymode_1_n1), .out(multiplexer_1_out), .sel(IsEasy));
  Multiplexer #(.width(4)) multiplexer_2 (
    .in0(hardmode_1_n2), .in1(easymode_1_n2), .out(multiplexer_2_out), .sel(IsEasy));
  Multiplexer #(.width(4)) multiplexer_3 (
    .in0(hardmode_1_n3), .in1(easymode_1_n3), .out(multiplexer_3_out), .sel(IsEasy));
  Multiplexer multiplexer_4 (
    .in0(hardmode_1_stop_out), .in1(easymode_1_stop_out), .out(multiplexer_4_out), .sel(IsEasy));
  Hex_Digit_Display hex_digit_display_1 (.value(multiplexer_1_out));  // open: dp
  Hex_Digit_Display hex_digit_display_2 (.value(multiplexer_2_out));  // open: dp
  Hex_Digit_Display hex_digit_display_3 (.value(multiplexer_3_out));  // open: dp
  Multiplexer #(.select(2), .width(4)) multiplexer_5 (
    .in0(multiplexer_1_out), .in1(multiplexer_2_out), .in2(multiplexer_3_out), .in3(4'b0000),
    .out(multiplexer_5_out), .sel(counter1_1_out1));
  _7447 #(.ShowInternalStructure("true")) u_7447_1 (
    .pin1(multiplexer_5_out[1]), .pin2(multiplexer_5_out[2]), .pin3(n7447_1_pin3), .pin4(n7447_1_pin3),
    .pin5(n7447_1_pin3), .pin6(multiplexer_5_out[3]), .pin7(multiplexer_5_out[0]), .pin15(F), .pin14(G),
    .pin13(A), .pin12(B), .pin11(C), .pin10(D), .pin9(E));
  LED LED1 (.in(jackpot_1_outp));
  Jackpot jackpot_1 (
    .N1(multiplexer_1_out), .N2(multiplexer_2_out), .N3(multiplexer_3_out), .Stop(multiplexer_4_out),
    .Outp(jackpot_1_outp));
  // also tied to VCC on the sheet: n7447_1_pin3
endmodule

module RNG4 (
  input  trigger,
  input  Clk,
  output [3:0] N1,
  output [3:0] N2,
  output [3:0] N3
);

  wire d_ff_2_q, d_ff_7_q, d_ff_12_q, d_ff_16_q, or_1_out, xor_1_out, xor_2_out, xor_3_out;

  or or_1 (or_1_out, d_ff_16_q, trigger);
  xor xor_1 (xor_1_out, d_ff_16_q, N3[2]);
  D_Flip_Flop d_ff_1 (.D(or_1_out), .clk(Clk), .Q(N1[3]), .preset(1'b0), .reset(1'b0));  // open: Qn
  D_Flip_Flop d_ff_2 (.D(N1[0]), .clk(Clk), .Q(d_ff_2_q), .preset(1'b0), .reset(1'b0));  // open: Qn
  D_Flip_Flop d_ff_3 (.D(N2[1]), .clk(Clk), .Q(N2[0]), .preset(1'b0), .reset(1'b0));  // open: Qn
  D_Flip_Flop d_ff_4 (.D(xor_1_out), .clk(Clk), .Q(N3[1]), .preset(1'b0), .reset(1'b0));  // open: Qn
  xor xor_2 (xor_2_out, d_ff_16_q, N1[3]);
  D_Flip_Flop d_ff_5 (.D(xor_2_out), .clk(Clk), .Q(N1[2]), .preset(1'b0), .reset(1'b0));  // open: Qn
  D_Flip_Flop d_ff_6 (.D(d_ff_2_q), .clk(Clk), .Q(N2[3]), .preset(1'b0), .reset(1'b0));  // open: Qn
  D_Flip_Flop d_ff_7 (.D(N2[0]), .clk(Clk), .Q(d_ff_7_q), .preset(1'b0), .reset(1'b0));  // open: Qn
  D_Flip_Flop d_ff_8 (.D(N3[1]), .clk(Clk), .Q(N3[0]), .preset(1'b0), .reset(1'b0));  // open: Qn
  D_Flip_Flop d_ff_9 (.D(N1[2]), .clk(Clk), .Q(N1[1]), .preset(1'b0), .reset(1'b0));  // open: Qn
  D_Flip_Flop d_ff_10 (.D(d_ff_7_q), .clk(Clk), .Q(N3[3]), .preset(1'b0), .reset(1'b0));  // open: Qn
  D_Flip_Flop d_ff_11 (.D(N2[3]), .clk(Clk), .Q(N2[2]), .preset(1'b0), .reset(1'b0));  // open: Qn
  D_Flip_Flop d_ff_12 (.D(N3[0]), .clk(Clk), .Q(d_ff_12_q), .preset(1'b0), .reset(1'b0));  // open: Qn
  xor xor_3 (xor_3_out, d_ff_16_q, N1[1]);
  D_Flip_Flop d_ff_13 (.D(xor_3_out), .clk(Clk), .Q(N1[0]), .preset(1'b0), .reset(1'b0));  // open: Qn
  D_Flip_Flop d_ff_14 (.D(N2[2]), .clk(Clk), .Q(N2[1]), .preset(1'b0), .reset(1'b0));  // open: Qn
  D_Flip_Flop d_ff_15 (.D(N3[3]), .clk(Clk), .Q(N3[2]), .preset(1'b0), .reset(1'b0));  // open: Qn
  D_Flip_Flop d_ff_16 (.D(d_ff_12_q), .clk(Clk), .Q(d_ff_16_q), .preset(1'b0), .reset(1'b0));  // open: Qn
endmodule

module EdgeDetector (
  input  inpt,
  input  Clk,
  output outp
);

  wire A_q, A_qn, and_1_out, and_2_out, and_3_out, B_q, B_qn, or_1_out, or_2_out;

  and and_1 (and_1_out, A_q, B_q, inpt);
  and and_2 (and_2_out, A_qn, inpt, B_qn);
  and and_3 (and_3_out, A_q, B_qn);
  and and_4 (outp, B_q, inpt, A_qn);
  or or_1 (or_1_out, outp, and_3_out, and_1_out);
  or or_2 (or_2_out, and_1_out, and_3_out, and_2_out);
  D_Flip_Flop A (.D(or_1_out), .clk(Clk), .Q(A_q), .Qn(A_qn), .preset(1'b0), .reset(1'b0));
  D_Flip_Flop B (.D(or_2_out), .clk(Clk), .Q(B_q), .Qn(B_qn), .preset(1'b0), .reset(1'b0));
endmodule

module Timer (
  input  Clock,
  input  enable,
  input  reset,
  output [3:0] Low,
  output [3:0] High,
  output enable_out
);

  wire and_1_out, and_2_out, and_4_out, not_1_out, not_2_out, not_3_out, not_4_out, not_5_out, not_6_out,
       not_7_out, not_8_out, or_1_out, or_2_out;

  Counter #(.max('hf), .width(4)) counter_1 (
    .load(or_1_out), .D(4'b1111), .count(enable), .Q(Low), .up(1'b0), .clk(Clock), .clr(1'b0));  // open: carry
  or or_1 (or_1_out, reset, and_2_out);
  not not_1 (not_1_out, Low[3]);
  not not_2 (not_2_out, Low[2]);
  not not_3 (not_3_out, Low[1]);
  not not_4 (not_4_out, Low[0]);
  and and_1 (and_1_out, not_1_out, not_2_out, not_3_out, not_4_out);
  and and_2 (and_2_out, enable, and_1_out);
  Counter #(.max('hf), .width(4)) counter_2 (
    .load(or_2_out), .D(4'b1111), .count(and_2_out), .Q(High), .up(1'b0), .clk(Clock), .clr(1'b0));  // open: carry
  not not_5 (not_5_out, High[3]);
  or or_2 (or_2_out, reset, enable_out);
  and and_3 (enable_out, and_2_out, and_4_out);
  not not_6 (not_6_out, High[2]);
  not not_7 (not_7_out, High[1]);
  not not_8 (not_8_out, High[0]);
  and and_4 (and_4_out, not_5_out, not_6_out, not_7_out, not_8_out);
endmodule

module counter1 (
  input  Clock,
  output Out1,
  output Out2
);

  wire d_ff_2_qn, xor_1_out;

  D_Flip_Flop d_ff_1 (.D(xor_1_out), .clk(Clock), .Q(Out2), .preset(1'b0), .reset(1'b0));  // open: Qn
  xor xor_1 (xor_1_out, Out2, Out1);
  D_Flip_Flop d_ff_2 (.D(d_ff_2_qn), .clk(Clock), .Q(Out1), .Qn(d_ff_2_qn), .preset(1'b0), .reset(1'b0));
endmodule

module easymode (
  input  Start,
  input  Clk,
  input  Stop,
  output [3:0] N1,
  output [3:0] N2,
  output [3:0] N3,
  output stop_out
);

  wire and_1_out, and_2_out, and_3_out, and_4_out, and_5_out, and_6_out, d_ff_1_q, d_ff_1_qn, d_ff_2_q,
       d_ff_2_qn, d_ff_3_qn, EdgeDetector_1_outp, EdgeDetector_2_outp, not_1_out, or_1_out, or_2_out,
       or_3_out, Timer_1_enable_out, Timer_2_enable_out;
  wire [3:0] rng3_1_n1, rng3_2_n2, rng3_3_n3;

  EdgeDetector EdgeDetector_2 (.inpt(Stop), .Clk(Clk), .outp(EdgeDetector_2_outp));
  EdgeDetector EdgeDetector_1 (.inpt(Start), .Clk(Clk), .outp(EdgeDetector_1_outp));
  or or_1 (or_1_out, and_1_out, and_2_out);
  and and_1 (and_1_out, not_1_out, d_ff_1_q);
  and and_2 (and_2_out, not_1_out, EdgeDetector_2_outp, d_ff_1_qn);
  D_Flip_Flop d_ff_1 (.D(or_1_out), .clk(Clk), .Q(d_ff_1_q), .Qn(d_ff_1_qn), .preset(1'b0), .reset(1'b0));
  or or_2 (or_2_out, and_3_out, and_4_out);
  or or_3 (or_3_out, and_5_out, and_6_out);
  not not_1 (not_1_out, EdgeDetector_1_outp);
  Timer Timer_1 (
    .Clock(Clk), .enable(d_ff_1_q), .reset(EdgeDetector_2_outp), .enable_out(Timer_1_enable_out));  // open: Low, High
  and and_3 (and_3_out, not_1_out, d_ff_2_q);
  and and_4 (and_4_out, not_1_out, Timer_1_enable_out, d_ff_2_qn);
  D_Flip_Flop d_ff_2 (.D(or_2_out), .clk(Clk), .Q(d_ff_2_q), .Qn(d_ff_2_qn), .preset(1'b0), .reset(1'b0));
  Timer Timer_2 (
    .Clock(Clk), .enable(d_ff_2_q), .reset(Timer_1_enable_out), .enable_out(Timer_2_enable_out));  // open: Low, High
  and and_5 (and_5_out, not_1_out, stop_out);
  and and_6 (and_6_out, not_1_out, Timer_2_enable_out, d_ff_3_qn);
  D_Flip_Flop d_ff_3 (.D(or_3_out), .clk(Clk), .Q(stop_out), .Qn(d_ff_3_qn), .preset(1'b0), .reset(1'b0));
  Register #(.width(4)) register_1 (.D(rng3_1_n1), .en(d_ff_1_qn), .clk(Clk), .Q(N1));  // open: clr
  RNG3 rng3_1 (.trigger(EdgeDetector_1_outp), .Clk(Clk), .N1(rng3_1_n1));  // open: N2, N3
  RNG3 rng3_2 (.trigger(EdgeDetector_1_outp), .Clk(Clk), .N2(rng3_2_n2));  // open: N1, N3
  RNG3 rng3_3 (.trigger(EdgeDetector_1_outp), .Clk(Clk), .N3(rng3_3_n3));  // open: N1, N2
  Register #(.width(4)) register_2 (.D(rng3_2_n2), .en(d_ff_2_qn), .clk(Clk), .Q(N2));  // open: clr
  Register #(.width(4)) register_3 (.D(rng3_3_n3), .en(d_ff_3_qn), .clk(Clk), .Q(N3));  // open: clr
endmodule

module Jackpot (
  input  [3:0] N1,
  input  [3:0] N2,
  input  [3:0] N3,
  input  Stop,
  output Outp
);

  wire and_1_out, and_2_out, and_3_out, and_4_out, nor_1_out, nor_2_out, nor_3_out, nor_4_out, or_1_out,
       or_2_out, or_3_out, or_4_out;

  and and_1 (and_1_out, N1[0], N2[0], N3[0]);
  and and_2 (and_2_out, N1[1], N2[1], N3[1]);
  and and_3 (and_3_out, N2[2], N1[2], N3[2]);
  and and_4 (and_4_out, N1[3], N2[3], N3[3]);
  or or_1 (or_1_out, and_1_out, nor_1_out);
  nor nor_1 (nor_1_out, N1[0], N3[0], N2[0]);
  nor nor_2 (nor_2_out, N1[1], N2[1], N3[1]);
  or or_2 (or_2_out, nor_2_out, and_2_out);
  or or_3 (or_3_out, and_3_out, nor_3_out);
  nor nor_3 (nor_3_out, N2[2], N1[2], N3[2]);
  nor nor_4 (nor_4_out, N1[3], N3[3], N2[3]);
  or or_4 (or_4_out, nor_4_out, and_4_out);
  and and_5 (Outp, or_1_out, or_2_out, or_3_out, Stop, or_4_out);
endmodule

module RNG3 (
  input  trigger,
  input  Clk,
  output [3:0] N1,
  output [3:0] N2,
  output [3:0] N3
);

  wire d_ff_1_q, d_ff_2_q, d_ff_5_q, d_ff_6_q, d_ff_7_q, d_ff_10_q, d_ff_11_q, d_ff_12_q, d_ff_15_q,
       d_ff_16_q, or_1_out, xor_1_out, xor_2_out, xor_3_out;

  or or_1 (or_1_out, d_ff_16_q, trigger);
  xor xor_1 (xor_1_out, d_ff_16_q, d_ff_15_q);
  D_Flip_Flop d_ff_1 (.D(or_1_out), .clk(Clk), .Q(d_ff_1_q), .preset(1'b0), .reset(1'b0));  // open: Qn
  D_Flip_Flop d_ff_2 (.D(N1[0]), .clk(Clk), .Q(d_ff_2_q), .preset(1'b0), .reset(1'b0));  // open: Qn
  D_Flip_Flop d_ff_3 (.D(N2[1]), .clk(Clk), .Q(N2[0]), .preset(1'b0), .reset(1'b0));  // open: Qn
  D_Flip_Flop d_ff_4 (.D(xor_1_out), .clk(Clk), .Q(N3[1]), .preset(1'b0), .reset(1'b0));  // open: Qn
  xor xor_2 (xor_2_out, d_ff_16_q, d_ff_1_q);
  D_Flip_Flop d_ff_5 (.D(xor_2_out), .clk(Clk), .Q(d_ff_5_q), .preset(1'b0), .reset(1'b0));  // open: Qn
  D_Flip_Flop d_ff_6 (.D(d_ff_2_q), .clk(Clk), .Q(d_ff_6_q), .preset(1'b0), .reset(1'b0));  // open: Qn
  D_Flip_Flop d_ff_7 (.D(N2[0]), .clk(Clk), .Q(d_ff_7_q), .preset(1'b0), .reset(1'b0));  // open: Qn
  D_Flip_Flop d_ff_8 (.D(N3[1]), .clk(Clk), .Q(N3[0]), .preset(1'b0), .reset(1'b0));  // open: Qn
  D_Flip_Flop d_ff_9 (.D(d_ff_5_q), .clk(Clk), .Q(N1[1]), .preset(1'b0), .reset(1'b0));  // open: Qn
  D_Flip_Flop d_ff_10 (.D(d_ff_7_q), .clk(Clk), .Q(d_ff_10_q), .preset(1'b0), .reset(1'b0));  // open: Qn
  D_Flip_Flop d_ff_11 (.D(d_ff_6_q), .clk(Clk), .Q(d_ff_11_q), .preset(1'b0), .reset(1'b0));  // open: Qn
  D_Flip_Flop d_ff_12 (.D(N3[0]), .clk(Clk), .Q(d_ff_12_q), .preset(1'b0), .reset(1'b0));  // open: Qn
  xor xor_3 (xor_3_out, d_ff_16_q, N1[1]);
  D_Flip_Flop d_ff_13 (.D(xor_3_out), .clk(Clk), .Q(N1[0]), .preset(1'b0), .reset(1'b0));  // open: Qn
  D_Flip_Flop d_ff_14 (.D(d_ff_11_q), .clk(Clk), .Q(N2[1]), .preset(1'b0), .reset(1'b0));  // open: Qn
  D_Flip_Flop d_ff_15 (.D(d_ff_10_q), .clk(Clk), .Q(d_ff_15_q), .preset(1'b0), .reset(1'b0));  // open: Qn
  D_Flip_Flop d_ff_16 (.D(d_ff_12_q), .clk(Clk), .Q(d_ff_16_q), .preset(1'b0), .reset(1'b0));  // open: Qn

  assign N1[3:2] = 2'b00;
  assign N2[3:2] = 2'b00;
  assign N3[3:2] = 2'b00;
endmodule

module hardmode (
  input  Start,
  input  Clk,
  input  Stop,
  output [3:0] N1,
  output [3:0] N2,
  output [3:0] N3,
  output stop_out
);

  wire and_1_out, and_2_out, and_3_out, and_4_out, and_5_out, and_6_out, d_ff_1_q, d_ff_1_qn, d_ff_2_q,
       d_ff_2_qn, d_ff_3_qn, EdgeDetector_1_outp, EdgeDetector_2_outp, not_1_out, or_1_out, or_2_out,
       or_3_out, Timer_1_enable_out, Timer_2_enable_out;
  wire [3:0] rng4_1_n1, rng4_2_n2, rng4_3_n3;

  EdgeDetector EdgeDetector_2 (.inpt(Stop), .Clk(Clk), .outp(EdgeDetector_2_outp));
  EdgeDetector EdgeDetector_1 (.inpt(Start), .Clk(Clk), .outp(EdgeDetector_1_outp));
  or or_1 (or_1_out, and_1_out, and_2_out);
  and and_1 (and_1_out, not_1_out, d_ff_1_q);
  and and_2 (and_2_out, not_1_out, EdgeDetector_2_outp, d_ff_1_qn);
  D_Flip_Flop d_ff_1 (.D(or_1_out), .clk(Clk), .Q(d_ff_1_q), .Qn(d_ff_1_qn), .preset(1'b0), .reset(1'b0));
  or or_2 (or_2_out, and_3_out, and_4_out);
  or or_3 (or_3_out, and_5_out, and_6_out);
  not not_1 (not_1_out, EdgeDetector_1_outp);
  Timer Timer_1 (
    .Clock(Clk), .enable(d_ff_1_q), .reset(EdgeDetector_2_outp), .enable_out(Timer_1_enable_out));  // open: Low, High
  and and_3 (and_3_out, not_1_out, d_ff_2_q);
  and and_4 (and_4_out, not_1_out, Timer_1_enable_out, d_ff_2_qn);
  D_Flip_Flop d_ff_2 (.D(or_2_out), .clk(Clk), .Q(d_ff_2_q), .Qn(d_ff_2_qn), .preset(1'b0), .reset(1'b0));
  Timer Timer_2 (
    .Clock(Clk), .enable(d_ff_2_q), .reset(Timer_1_enable_out), .enable_out(Timer_2_enable_out));  // open: Low, High
  and and_5 (and_5_out, not_1_out, stop_out);
  and and_6 (and_6_out, not_1_out, Timer_2_enable_out, d_ff_3_qn);
  D_Flip_Flop d_ff_3 (.D(or_3_out), .clk(Clk), .Q(stop_out), .Qn(d_ff_3_qn), .preset(1'b0), .reset(1'b0));
  Register #(.width(4)) register_1 (.D(rng4_1_n1), .en(d_ff_1_qn), .clk(Clk), .Q(N1));  // open: clr
  RNG4 rng4_1 (.trigger(EdgeDetector_1_outp), .Clk(Clk), .N1(rng4_1_n1));  // open: N2, N3
  RNG4 rng4_2 (.trigger(EdgeDetector_1_outp), .Clk(Clk), .N2(rng4_2_n2));  // open: N1, N3
  RNG4 rng4_3 (.trigger(EdgeDetector_1_outp), .Clk(Clk), .N3(rng4_3_n3));  // open: N1, N2
  Register #(.width(4)) register_2 (.D(rng4_2_n2), .en(d_ff_2_qn), .clk(Clk), .Q(N2));  // open: clr
  Register #(.width(4)) register_3 (.D(rng4_3_n3), .en(d_ff_3_qn), .clk(Clk), .Q(N3));  // open: clr
endmodule
